# Fritzing sketch keyboard (saved by Fritzing 0.9.3b)
circuit board: 1.5cm x 1.5cm
circuit board: 1.5cm x 1.5cm
circuit board: 1.5cm x 1.5cm
circuit board: 1.5cm x 1.5cm
circuit board: 1.5cm x 1.5cm
circuit board: 1.5cm x 1.5cm
circuit board: 1.5cm x 1.5cm
circuit board: 1.5cm x 1.5cm
circuit board: 1.5cm x 1.5cm
circuit board: 1.5cm x 1.5cm
circuit board: 1.5cm x 1.5cm
circuit board: 1.5cm x 1.5cm
circuit board: 1.5cm x 1.5cm
circuit board: 1.5cm x 1.5cm
circuit board: 1.5cm x 1.5cm
circuit board: 1.5cm x 1.5cm
circuit board: 1.5cm x 1.5cm
circuit board: 1.5cm x 1.5cm
circuit board: 1.5cm x 1.5cm
circuit board: 1.5cm x 1.5cm
circuit board: 1.5cm x 1.5cm
circuit board: 1.5cm x 1.5cm
circuit board: 1.5cm x 1.5cm
circuit board: 1.5cm x 1.5cm
circuit board: 1.5cm x 1.5cm
circuit board: 1.5cm x 1.5cm
circuit board: 1.5cm x 1.5cm
circuit board: 1.5cm x 1.5cm
circuit board: 1.5cm x 1.5cm
circuit board: 1.5cm x 1.5cm
circuit board: 1.5cm x 1.5cm
circuit board: 1.5cm x 1.5cm
circuit board: 49.3738cm x 11.192cm
circuit board: 1.5cm x 1.5cm
circuit board: 1.5cm x 1.5cm
circuit board: 1.5cm x 1.5cm
circuit board: 1.5cm x 1.5cm
circuit board: 1.5cm x 1.5cm
circuit board: 1.5cm x 1.5cm
circuit board: 1.5cm x 1.5cm
circuit board: 1.5cm x 1.5cm
circuit board: 1.5cm x 1.5cm
circuit board: 1.5cm x 1.5cm
circuit board: 1.5cm x 1.5cm
circuit board: 1.5cm x 1.5cm
circuit board: 1.5cm x 1.5cm
circuit board: 1.5cm x 1.5cm
circuit board: 1.5cm x 1.5cm
circuit board: 1.5cm x 1.5cm
circuit board: 1.5cm x 1.5cm
circuit board: 1.5cm x 1.5cm
circuit board: 1.5cm x 1.5cm
circuit board: 1.5cm x 1.5cm
circuit board: 1.5cm x 1.5cm
circuit board: 1.5cm x 1.5cm
circuit board: 1.5cm x 1.5cm
circuit board: 1.5cm x 1.5cm
circuit board: 1.5cm x 1.5cm
circuit board: 1.5cm x 1.5cm
circuit board: 1.5cm x 1.5cm
circuit board: 1.5cm x 1.5cm
circuit board: 1.5cm x 1.5cm
circuit board: 1.5cm x 1.5cm
circuit board: 1.5cm x 1.5cm
circuit board: 1.5cm x 1.5cm
circuit board: 1.5cm x 1.5cm
circuit board: 1.5cm x 1.5cm
circuit board: 1.5cm x 1.5cm
circuit board: 1.5cm x 1.5cm
circuit board: 1.5cm x 1.5cm
circuit board: 1.5cm x 1.5cm
circuit board: 1.5cm x 1.5cm
circuit board: 1.5cm x 1.5cm
circuit board: 1.5cm x 1.5cm
circuit board: 1.5cm x 1.5cm
circuit board: 1.5cm x 1.5cm
circuit board: 1.5cm x 1.5cm
circuit board: 1.5cm x 1.5cm
circuit board: 1.5cm x 1.5cm
circuit board: 1.5cm x 1.5cm
circuit board: 1.5cm x 1.5cm
circuit board: 1.5cm x 1.5cm
circuit board: 1.5cm x 1.5cm
circuit board: 1.5cm x 1.5cm
circuit board: 1.5cm x 1.5cm
circuit board: 1.5cm x 1.5cm
circuit board: 1.5cm x 1.5cm
circuit board: 1.5cm x 1.5cm
circuit board: 1.5cm x 1.5cm
circuit board: 1.5cm x 1.5cm
circuit board: 1.5cm x 1.5cm
circuit board: 1.5cm x 1.5cm
circuit board: 1.5cm x 1.5cm
circuit board: 1.5cm x 1.5cm
circuit board: 1.5cm x 1.5cm
circuit board: 1.5cm x 1.5cm
circuit board: 1.5cm x 1.5cm
circuit board: 1.5cm x 1.5cm
circuit board: 1.5cm x 1.5cm
circuit board: 1.5cm x 1.5cm
circuit board: 1.5cm x 1.5cm
circuit board: 1.5cm x 1.5cm
circuit board: 4.58931cm x 9.82459cm
circuit board: 1.5cm x 1.5cm
circuit board: 1.5cm x 1.5cm
circuit board: 1.5cm x 1.5cm
circuit board: 1.5cm x 1.5cm
circuit board: 1.5cm x 1.5cm
circuit board: 1.5cm x 1.5cm
circuit board: 1.5cm x 1.5cm
circuit board: 1.5cm x 1.5cm
circuit board: 1.5cm x 1.5cm
circuit board: 1.5cm x 1.5cm
circuit board: 1.5cm x 1.5cm
circuit board: 1.5cm x 1.5cm
circuit board: 1.5cm x 1.5cm
circuit board: 1.5cm x 1.5cm
circuit board: 1.5cm x 1.5cm
circuit board: 1.5cm x 1.5cm
circuit board: 1.5cm x 1.5cm
circuit board: 1.5cm x 1.5cm
circuit board: 1.5cm x 1.5cm
breadboards: 1

parts:
  KEY_TILDA = Cherry MX Keyswitch
  KEY_1 = Cherry MX Keyswitch
  KEY_2 = Cherry MX Keyswitch
  KEY_3 = Cherry MX Keyswitch
  KEY_4 = Cherry MX Keyswitch
  KEY_5 = Cherry MX Keyswitch
  KEY_6 = Cherry MX Keyswitch
  KEY_7 = Cherry MX Keyswitch
  KEY_8 = Cherry MX Keyswitch
  KEY_9 = Cherry MX Keyswitch
  KEY_0 = Cherry MX Keyswitch
  KEY_- = Cherry MX Keyswitch
  KEY_+ = Cherry MX Keyswitch
  KEY_Q = Cherry MX Keyswitch
  KEY_W = Cherry MX Keyswitch
  KEY_R = Cherry MX Keyswitch
  KEY_E = Cherry MX Keyswitch
  KEY_T = Cherry MX Keyswitch
  KEY_Y = Cherry MX Keyswitch
  KEY_U = Cherry MX Keyswitch
  KEY_I = Cherry MX Keyswitch
  KEY_O = Cherry MX Keyswitch
  KEY_[ = Cherry MX Keyswitch
  KEY_P = Cherry MX Keyswitch
  KEY_] = Cherry MX Keyswitch
  KEY_J = Cherry MX Keyswitch
  KEY_K = Cherry MX Keyswitch
  KEY_H = Cherry MX Keyswitch
  KEY_D = Cherry MX Keyswitch
  KEY_; = Cherry MX Keyswitch
  KEY_A = Cherry MX Keyswitch
  KEY_L = Cherry MX Keyswitch
  KEY_' = Cherry MX Keyswitch
  KEY_F = Cherry MX Keyswitch
  KEY_S = Cherry MX Keyswitch
  KEY_G = Cherry MX Keyswitch
  KEY_V = Cherry MX Keyswitch
  KEY_X = Cherry MX Keyswitch
  KEY = Cherry MX Keyswitch
  KEY_N = Cherry MX Keyswitch
  KEY_2 = Cherry MX Keyswitch
  KEY_Z = Cherry MX Keyswitch
  KEY_M = Cherry MX Keyswitch
  KEY_C = Cherry MX Keyswitch
  KEY_/ = Cherry MX Keyswitch
  KEY_B = Cherry MX Keyswitch
  KEY_ESC = Cherry MX Keyswitch
  KEY_F1 = Cherry MX Keyswitch
  KEY_F3 = Cherry MX Keyswitch
  KEY_F2 = Cherry MX Keyswitch
  KEY_F4 = Cherry MX Keyswitch
  KEY_F5 = Cherry MX Keyswitch
  KEY_F7 = Cherry MX Keyswitch
  KEY_F6 = Cherry MX Keyswitch
  KEY_F8 = Cherry MX Keyswitch
  KEY_F12 = Cherry MX Keyswitch
  KEY_F9 = Cherry MX Keyswitch
  KEY_F11 = Cherry MX Keyswitch
  KEY_F10 = Cherry MX Keyswitch
  KEY_FUN2 = Cherry MX Keyswitch
  KEY_FUN1 = Cherry MX Keyswitch
  KEY_FUN3 = Cherry MX Keyswitch
  KEY_FUN4 = Cherry MX Keyswitch
  KEY_FUN6 = Cherry MX Keyswitch
  KEY_FUN5 = Cherry MX Keyswitch
  KEY_FUN7 = Cherry MX Keyswitch
  KEY_FUN8 = Cherry MX Keyswitch
  KEY_FUN9 = Cherry MX Keyswitch
  KEY_FUN10 = Cherry MX Keyswitch
  KEY_TAB = Cherry MX Keyswitch
  KEY_CAPLOCK = Cherry MX Keyswitch  # not connected
  KEY_SHIFT = Cherry MX Keyswitch
  KEY_CTRL = Cherry MX Keyswitch
  KEY_OS = Cherry MX Keyswitch
  KEY_ALT = Cherry MX Keyswitch
  KEY_DOWN = Cherry MX Keyswitch
  KEY_LEFT = Cherry MX Keyswitch
  KEY_UP = Cherry MX Keyswitch
  KEY_FUN14 = Cherry MX Keyswitch
  KEY_FUN15 = Cherry MX Keyswitch
  KEY_FUN16 = Cherry MX Keyswitch
  KEY_FUN17 = Cherry MX Keyswitch
  KEY_FUN18 = Cherry MX Keyswitch
  KEY_FUN19 = Cherry MX Keyswitch
  KEY_FUN20 = Cherry MX Keyswitch
  KEY_RIGHT = Cherry MX Keyswitch
  KEY_FUN22 = Cherry MX Keyswitch
  KEY_FUN23 = Cherry MX Keyswitch
  KEY_FUN24 = Cherry MX Keyswitch
  KEY_FUN25 = Cherry MX Keyswitch
  KEY_3 = Cherry MX Keyswitch
  KEY_0_2 = Cherry MX Keyswitch
  KEY_2_2 = Cherry MX Keyswitch
  KEY_3_2 = Cherry MX Keyswitch
  KEY_1_2 = Cherry MX Keyswitch
  KEY_4_2 = Cherry MX Keyswitch
  KEY_6_2 = Cherry MX Keyswitch
  KEY_5_2 = Cherry MX Keyswitch
  KEY_9_2 = Cherry MX Keyswitch
  KEY_FUN36 = Cherry MX Keyswitch
  KEY_7_2 = Cherry MX Keyswitch
  KEY_NUMLOCK = Cherry MX Keyswitch
  KEY_* = Cherry MX Keyswitch
  KEY_-_2 = Cherry MX Keyswitch
  KEY_ENTER = Cherry MX Keyswitch
  KEY_+_2 = Cherry MX Keyswitch
  KEY_-_3 = Cherry MX Keyswitch
  KEY_PRTSCR = Cherry MX Keyswitch
  KEY_BREAK = Cherry MX Keyswitch
  KEY_SCRLCK = Cherry MX Keyswitch
  KEY_FUN37 = Cherry MX Keyswitch
  KEY_FUN38 = Cherry MX Keyswitch
  KEY_FUN39 = Cherry MX Keyswitch
  KEY_FUN40 = Cherry MX Keyswitch
  KEY_FUN41 = Cherry MX Keyswitch
  KEY_FUN42 = Cherry MX Keyswitch
  KEY_FUN43 = Cherry MX Keyswitch
  KEY_FUN44 = Cherry MX Keyswitch
  KEY_FUN45 = Cherry MX Keyswitch
  KEY_FUN46 = Cherry MX Keyswitch

nets:
  N1: KEY_TILDA.pin_4, KEY_1.pin_4, KEY_2.pin_4, KEY_3.pin_4, KEY_4.pin_4, KEY_5.pin_4, KEY_6.pin_4, KEY_7.pin_4, KEY_8.pin_4, KEY_9.pin_4, KEY_0.pin_4, KEY_-.pin_4, KEY_+.pin_4, KEY_FUN2.pin_4, KEY_FUN1.pin_4, KEY_FUN19.pin_4, KEY_FUN20.pin_4, KEY_FUN25.pin_4, KEY_NUMLOCK.pin_4, KEY_*.pin_4, KEY_-_2.pin_4, KEY_-_3.pin_4
  N2: KEY_Q.pin_4, KEY_W.pin_4, KEY_R.pin_4, KEY_E.pin_4, KEY_T.pin_4, KEY_Y.pin_4, KEY_U.pin_4, KEY_I.pin_4, KEY_O.pin_4, KEY_[.pin_4, KEY_P.pin_4, KEY_].pin_4, KEY_FUN3.pin_4, KEY_FUN4.pin_4, KEY_TAB.pin_4, KEY_FUN17.pin_4, KEY_FUN18.pin_4, KEY_FUN24.pin_4, KEY_9_2.pin_4, KEY_FUN36.pin_4, KEY_7_2.pin_4
  N3: KEY_J.pin_4, KEY_K.pin_4, KEY_H.pin_4, KEY_D.pin_4, KEY_;.pin_4, KEY_A.pin_4, KEY_L.pin_4, KEY_'.pin_4, KEY_F.pin_4, KEY_S.pin_4, KEY_G.pin_4, KEY_FUN6.pin_4, KEY_FUN5.pin_4, KEY_FUN15.pin_4, KEY_FUN16.pin_4, KEY_FUN23.pin_4, KEY_4_2.pin_4, KEY_6_2.pin_4, KEY_5_2.pin_4, KEY_+_2.pin_4
  N4: KEY_V.pin_4, KEY_X.pin_4, KEY.pin_4, KEY_N.pin_4, KEY_2.pin_4, KEY_Z.pin_4, KEY_M.pin_4, KEY_C.pin_4, KEY_/.pin_4, KEY_B.pin_4, KEY_FUN7.pin_4, KEY_FUN8.pin_4, KEY_SHIFT.pin_4, KEY_UP.pin_4, KEY_FUN14.pin_4, KEY_FUN22.pin_4, KEY_2_2.pin_4, KEY_3_2.pin_4, KEY_1_2.pin_4
  N5: KEY_ESC.pin_4, KEY_F1.pin_4, KEY_F3.pin_4, KEY_F2.pin_4, KEY_F4.pin_4, KEY_F5.pin_4, KEY_F7.pin_4, KEY_F6.pin_4, KEY_F8.pin_4, KEY_F12.pin_4, KEY_F9.pin_4, KEY_F11.pin_4, KEY_F10.pin_4, KEY_PRTSCR.pin_4, KEY_BREAK.pin_4, KEY_SCRLCK.pin_4
  N6: KEY_FUN2.pin_2, KEY_FUN4.pin_2, KEY_FUN6.pin_2, KEY_FUN8.pin_2, KEY_FUN10.pin_2
  N7: KEY_FUN1.pin_2, KEY_FUN3.pin_2, KEY_FUN5.pin_2, KEY_FUN7.pin_2, KEY_FUN9.pin_2
  N8: KEY_FUN9.pin_4, KEY_FUN10.pin_4, KEY_CTRL.pin_4, KEY_OS.pin_4, KEY_ALT.pin_4, KEY_DOWN.pin_4, KEY_LEFT.pin_4, KEY_RIGHT.pin_4, KEY_3.pin_4, KEY_0_2.pin_4, KEY_ENTER.pin_4
  N9: KEY_FUN37.pin_2, KEY_FUN39.pin_2, KEY_FUN42.pin_2, KEY_FUN43.pin_2, KEY_FUN46.pin_2
  N10: KEY_FUN37.pin_4, KEY_FUN38.pin_4
  N11: KEY_FUN38.pin_2, KEY_FUN40.pin_2, KEY_FUN41.pin_2, KEY_FUN44.pin_2, KEY_FUN45.pin_2
  N12: KEY_FUN39.pin_4, KEY_FUN40.pin_4
  N13: KEY_FUN41.pin_4, KEY_FUN42.pin_4
  N14: KEY_FUN43.pin_4, KEY_FUN44.pin_4

notes:
  Keyboard
  v0.1
