# Fritzing sketch keyboard_numpad (saved by Fritzing 0.9.3b)
circuit board: 7.9cm x 9.8cm
breadboards: 1

parts:
  ROW = female pin header, 5 pins [form="♀ (female)"]
  COLUMN = female pin header, 4 pins [form="♀ (female)"]
  K_/ = Cherry MX Keyswitch
  K_* = Cherry MX Keyswitch
  K_- = Cherry MX Keyswitch
  K_7 = Cherry MX Keyswitch
  K_8 = Cherry MX Keyswitch
  K_9 = Cherry MX Keyswitch
  K_+ = Cherry MX Keyswitch
  K_6 = Cherry MX Keyswitch
  K_5 = Cherry MX Keyswitch
  K_4 = Cherry MX Keyswitch
  K_1 = Cherry MX Keyswitch
  K_2 = Cherry MX Keyswitch
  K_3 = Cherry MX Keyswitch
  K_0 = Cherry MX Keyswitch
  K = Cherry MX Keyswitch
  K_ENTER = Cherry MX Keyswitch
  D1 = Diode [package=diode-1n4148]
  D2 = Diode [package=diode-1n4148]
  D3 = Diode [package=diode-1n4148]
  D4 = Diode [package=diode-1n4148]
  D5 = Diode [package=diode-1n4148]
  D6 = Diode [package=diode-1n4148]
  D8 = Diode [package=diode-1n4148]
  D7 = Diode [package=diode-1n4148]
  D11 = Diode [package=diode-1n4148]
  D10 = Diode [package=diode-1n4148]
  D9 = Diode [package=diode-1n4148]
  D15 = Diode [package=diode-1n4148]
  D12 = Diode [package=diode-1n4148]
  D13 = Diode [package=diode-1n4148]
  D14 = Diode [package=diode-1n4148]
  D17 = Diode [package=diode-1n4148]
  D16 = Diode [package=diode-1n4148]
  K_NUMLOCK = Cherry MX Keyswitch
  LED_COL1 = female pin header, 6 pins [form="♀ (female)"]
  LED_COL2 = female pin header, 3 pins [form="♀ (female)"]
  LED_COL3 = female pin header, 3 pins [form="♀ (female)"]
  LED_ROW = female pin header, 5 pins [form="♀ (female)"]
  K_PS_LED = female pin header, 3 pins [form="♀ (female)"]
  K_BRK_LED = female pin header, 3 pins [form="♀ (female)"]
  K_SL_LED = female pin header, 3 pins [form="♀ (female)"]
  K_BRK_ROW = female pin header, 1 pin [form="♀ (female)"]
  K_PS_ROW = female pin header, 1 pin [form="♀ (female)"]
  K_SL_ROW = female pin header, 1 pin [form="♀ (female)"]
  K_PS_COL = female pin header, 1 pin [form="♀ (female)"]
  K_PS_LED_ROW = female pin header, 1 pin [form="♀ (female)"]
  K_SL_LED_ROW = female pin header, 1 pin [form="♀ (female)"]
  K_SL_COL = female pin header, 1 pin [form="♀ (female)"]
  K_BRK_LED_ROW = female pin header, 1 pin [form="♀ (female)"]
  K_BRK_COL = female pin header, 1 pin [form="♀ (female)"]

nets:
  N1: ROW.pin1, D1.C, D2.C, D3.C, D4.C
  N2: ROW.pin2, D5.C, D6.C, D8.C, D7.C
  N3: ROW.pin3, D11.C, D10.C, D9.C, K_BRK_ROW.pin1
  N4: ROW.pin4, D15.C, D12.C, D13.C, D14.C
  N5: ROW.pin5, D17.C, D16.C, K_PS_ROW.pin1, K_SL_ROW.pin1
  N6: COLUMN.pin1, K_7.pin_2, K_4.pin_2, K_1.pin_2, K_0.pin_2, K_NUMLOCK.pin_2
  N7: COLUMN.pin2, K_/.pin_2, K_8.pin_2, K_5.pin_2, K_2.pin_2, K_PS_COL.pin1
  N8: COLUMN.pin3, K_*.pin_2, K_9.pin_2, K_6.pin_2, K_3.pin_2, K.pin_2
  N9: COLUMN.pin4, K_-.pin_2, K_+.pin_2, K_ENTER.pin_2, K_SL_COL.pin1, K_BRK_COL.pin1
  N10: K_/.pin_1, K_/.pin_6, K_*.pin_1, K_*.pin_6, K_-.pin_1, K_-.pin_6, K_7.pin_1, K_7.pin_6, K_8.pin_1, K_8.pin_6, K_9.pin_1, K_9.pin_6, K_+.pin_1, K_+.pin_6, K_6.pin_1, K_6.pin_6, K_5.pin_1, K_5.pin_6, K_4.pin_1, K_4.pin_6, K_1.pin_1, K_1.pin_6, K_2.pin_1, K_2.pin_6, K_3.pin_1, K_3.pin_6, K_0.pin_1, K_0.pin_6, K.pin_1, K.pin_6, K_ENTER.pin_1, K_ENTER.pin_6, K_NUMLOCK.pin_1, K_NUMLOCK.pin_6, LED_COL1.pin1, LED_COL1.pin4, LED_COL2.pin1, LED_COL3.pin1, LED_ROW.pin1, LED_ROW.pin2, LED_ROW.pin3, LED_ROW.pin4, LED_ROW.pin5, K_PS_LED.pin1, K_BRK_LED.pin1, K_SL_LED.pin1, K_PS_LED_ROW.pin1, K_SL_LED_ROW.pin1, K_BRK_LED_ROW.pin1
  N11: K_/.pin_3, D2.A
  N12: K_/.pin_4, K_/.pin_5, K_8.pin_4, K_8.pin_5, K_5.pin_4, K_5.pin_5, K_2.pin_4, K_2.pin_5, LED_COL1.pin5, LED_COL1.pin6, K_PS_LED.pin2, K_PS_LED.pin3
  N13: K_*.pin_3, D3.A
  N14: K_*.pin_4, K_*.pin_5, K_9.pin_4, K_9.pin_5, K_6.pin_4, K_6.pin_5, K_3.pin_4, K_3.pin_5, K.pin_4, K.pin_5, LED_COL2.pin2, LED_COL2.pin3
  N15: K_-.pin_3, D4.A
  N16: K_-.pin_4, K_-.pin_5, K_+.pin_4, K_+.pin_5, K_ENTER.pin_4, K_ENTER.pin_5, LED_COL3.pin2, LED_COL3.pin3, K_BRK_LED.pin2, K_BRK_LED.pin3, K_SL_LED.pin2, K_SL_LED.pin3
  N17: K_7.pin_3, D5.A
  N18: K_7.pin_4, K_7.pin_5, K_4.pin_4, K_4.pin_5, K_1.pin_4, K_1.pin_5, K_0.pin_4, K_0.pin_5, K_NUMLOCK.pin_4, K_NUMLOCK.pin_5, LED_COL1.pin2, LED_COL1.pin3
  N19: K_8.pin_3, D7.A
  N20: K_9.pin_3, D6.A
  N21: K_+.pin_3, D8.A
  N22: K_6.pin_3, D11.A
  N23: K_5.pin_3, D10.A
  N24: K_4.pin_3, D9.A
  N25: K_1.pin_3, D12.A
  N26: K_2.pin_3, D13.A
  N27: K_3.pin_3, D14.A
  N28: K_0.pin_3, D16.A
  N29: K.pin_3, D17.A
  N30: K_ENTER.pin_3, D15.A
  N31: D1.A, K_NUMLOCK.pin_3

notes:
  Num Pad
  v0.2

custom parts:
  Cherry MX Keyswitch: Cherry MX Keyswitch button for keyboards
