# Fritzing sketch keyboard_numpad_upper (saved by Fritzing 0.9.3b)
circuit board: 8cm x 1.9cm
breadboards: 1

parts:
  K_SCRLCK = Cherry MX Keyswitch
  K_PRNSCR = Cherry MX Keyswitch
  K_BREAK = Cherry MX Keyswitch
  D18 = Diode [package=diode-1n4148]
  D19 = Diode [package=diode-1n4148]
  D20 = Diode [package=diode-1n4148]
  K_BRK_ROW_COL = female pin header, 2 pins [form="♀ (female)"]
  K_PS_ROW_COL = female pin header, 2 pins [form="♀ (female)"]
  K_SL_ROW_COL = female pin header, 2 pins [form="♀ (female)"]
  K_SL_LED = female pin header, 4 pins [form="♀ (female)"]
  K_PS_LED = female pin header, 4 pins [form="♀ (female)"]
  K_BRK_LED = female pin header, 4 pins [form="♀ (female)"]

nets:
  N1: K_SCRLCK.pin_1, K_SCRLCK.pin_6, K_SL_LED.pin3, K_SL_LED.pin4
  N2: K_SCRLCK.pin_2, K_SL_ROW_COL.pin2
  N3: K_SCRLCK.pin_3, D18.A
  N4: K_SCRLCK.pin_4, K_SCRLCK.pin_5, K_SL_LED.pin1, K_SL_LED.pin2
  N5: K_PRNSCR.pin_1, K_PRNSCR.pin_6, K_PS_LED.pin3, K_PS_LED.pin4
  N6: K_PRNSCR.pin_2, K_PS_ROW_COL.pin2
  N7: K_PRNSCR.pin_3, D19.A
  N8: K_PRNSCR.pin_4, K_PRNSCR.pin_5, K_PS_LED.pin1, K_PS_LED.pin2
  N9: K_BREAK.pin_1, K_BREAK.pin_6, K_BRK_LED.pin3, K_BRK_LED.pin4
  N10: K_BREAK.pin_2, K_BRK_ROW_COL.pin2
  N11: K_BREAK.pin_3, D20.A
  N12: K_BREAK.pin_4, K_BREAK.pin_5, K_BRK_LED.pin1, K_BRK_LED.pin2
  N13: D18.C, K_SL_ROW_COL.pin1
  N14: D19.C, K_PS_ROW_COL.pin1
  N15: D20.C, K_BRK_ROW_COL.pin1

notes:
  Num Pad Upper
  v0.1

custom parts:
  Cherry MX Keyswitch: Cherry MX Keyswitch button for keyboards
