# Fritzing sketch keyboard_specfun (saved by Fritzing 0.9.3b)
circuit board: 3.7cm x 9cm
breadboards: 1

parts:
  KEY_FUN1 = Cherry MX Keyswitch
  KEY_FUN2 = Cherry MX Keyswitch
  KEY_FUN3 = Cherry MX Keyswitch
  KEY_FUN4 = Cherry MX Keyswitch
  KEY_FUN5 = Cherry MX Keyswitch
  KEY_FUN6 = Cherry MX Keyswitch
  KEY_FUN7 = Cherry MX Keyswitch
  KEY_FUN8 = Cherry MX Keyswitch
  KEY_FUN10 = Cherry MX Keyswitch
  KEY_FUN9 = Cherry MX Keyswitch
  D1 = Diode [package=diode-1n4148]
  D2 = Diode [package=diode-1n4148]
  D3 = Diode [package=diode-1n4148]
  D4 = Diode [package=diode-1n4148]
  D5 = Diode [package=diode-1n4148]
  D6 = Diode [package=diode-1n4148]
  D7 = Diode [package=diode-1n4148]
  D8 = Diode [package=diode-1n4148]
  D9 = Diode [package=diode-1n4148]
  D10 = Diode [package=diode-1n4148]
  COL1 = female pin header, 4 pins [form="♀ (female)"]
  COL2 = female pin header, 4 pins [form="♀ (female)"]
  ROW5 = female pin header, 2 pins [form="♀ (female)"]
  ROW4 = female pin header, 2 pins [form="♀ (female)"]
  ROW3 = female pin header, 2 pins [form="♀ (female)"]
  ROW2 = female pin header, 2 pins [form="♀ (female)"]
  ROW1 = female pin header, 2 pins [form="♀ (female)"]

nets:
  N1: KEY_FUN1.pin_1, KEY_FUN1.pin_6, KEY_FUN2.pin_1, KEY_FUN2.pin_6, KEY_FUN3.pin_1, KEY_FUN3.pin_6, KEY_FUN4.pin_1, KEY_FUN4.pin_6, KEY_FUN5.pin_1, KEY_FUN5.pin_6, KEY_FUN6.pin_1, KEY_FUN6.pin_6, KEY_FUN7.pin_1, KEY_FUN7.pin_6, KEY_FUN8.pin_1, KEY_FUN8.pin_6, KEY_FUN10.pin_1, KEY_FUN10.pin_6, KEY_FUN9.pin_1, KEY_FUN9.pin_6, COL1.pin2, COL2.pin2, ROW5.pin1, ROW4.pin1, ROW3.pin1, ROW2.pin1, ROW1.pin1
  N2: KEY_FUN1.pin_2, KEY_FUN3.pin_2, KEY_FUN5.pin_2, KEY_FUN7.pin_2, KEY_FUN9.pin_2, COL1.pin1
  N3: KEY_FUN1.pin_3, D1.A
  N4: KEY_FUN1.pin_4, KEY_FUN1.pin_5, KEY_FUN3.pin_4, KEY_FUN3.pin_5, KEY_FUN5.pin_4, KEY_FUN5.pin_5, KEY_FUN7.pin_4, KEY_FUN7.pin_5, KEY_FUN9.pin_4, KEY_FUN9.pin_5, COL1.pin3, COL1.pin4
  N5: KEY_FUN2.pin_2, KEY_FUN4.pin_2, KEY_FUN6.pin_2, KEY_FUN8.pin_2, KEY_FUN10.pin_2, COL2.pin1
  N6: KEY_FUN2.pin_3, D2.A
  N7: KEY_FUN2.pin_4, KEY_FUN2.pin_5, KEY_FUN4.pin_4, KEY_FUN4.pin_5, KEY_FUN6.pin_4, KEY_FUN6.pin_5, KEY_FUN8.pin_4, KEY_FUN8.pin_5, KEY_FUN10.pin_4, KEY_FUN10.pin_5, COL2.pin3, COL2.pin4
  N8: KEY_FUN3.pin_3, D4.A
  N9: KEY_FUN4.pin_3, D3.A
  N10: KEY_FUN5.pin_3, D6.A
  N11: KEY_FUN6.pin_3, D5.A
  N12: KEY_FUN7.pin_3, D8.A
  N13: KEY_FUN8.pin_3, D7.A
  N14: KEY_FUN10.pin_3, D9.A
  N15: KEY_FUN9.pin_3, D10.A
  N16: D1.C, D2.C, ROW1.pin2
  N17: D3.C, D4.C, ROW2.pin2
  N18: D5.C, D6.C, ROW3.pin2
  N19: D7.C, D8.C, ROW4.pin2
  N20: D9.C, D10.C, ROW5.pin2

custom parts:
  Cherry MX Keyswitch: Cherry MX Keyswitch button for keyboards
