# Fritzing sketch keyboard_specfun_v0.1 (saved by Fritzing 0.9.3b)
circuit board: 4cm x 10cm
breadboards: 1

parts:
  KEY_FUN10 = Cherry MX Keyswitch
  KEY_FUN9 = Cherry MX Keyswitch
  KEY_FUN7 = Cherry MX Keyswitch
  KEY_FUN5 = Cherry MX Keyswitch
  KEY_FUN6 = Cherry MX Keyswitch
  KEY_FUN4 = Cherry MX Keyswitch
  KEY_FUN3 = Cherry MX Keyswitch
  KEY_FUN1 = Cherry MX Keyswitch
  KEY_FUN2 = Cherry MX Keyswitch
  KEY_FUN8 = Cherry MX Keyswitch
  ROW = female pin header, 5 pins [form="♀ (female)"]
  COL = female pin header, 2 pins [form="♀ (female)"]
  LED1 = female pin header, 4 pins [form="♀ (female)"]
  LED2 = female pin header, 4 pins [form="♀ (female)"]

nets:
  N1: KEY_FUN10.pin_1, KEY_FUN10.pin_10, KEY_FUN6.pin_1, KEY_FUN6.pin_10, KEY_FUN4.pin_1, KEY_FUN4.pin_10, KEY_FUN2.pin_1, KEY_FUN2.pin_9, KEY_FUN2.pin_10, KEY_FUN8.pin_1, KEY_FUN8.pin_10, LED2.pin4
  N2: KEY_FUN10.pin_2, KEY_FUN9.pin_2, ROW.pin5
  N3: KEY_FUN10.pin_4, KEY_FUN6.pin_4, KEY_FUN4.pin_4, KEY_FUN2.pin_4, KEY_FUN8.pin_4, COL.pin1
  N4: KEY_FUN10.pin_6, KEY_FUN10.pin_7, KEY_FUN6.pin_6, KEY_FUN6.pin_7, KEY_FUN4.pin_6, KEY_FUN4.pin_7, KEY_FUN2.pin_6, KEY_FUN2.pin_7, KEY_FUN8.pin_6, KEY_FUN8.pin_7, LED2.pin1
  N5: KEY_FUN9.pin_1, KEY_FUN9.pin_9, KEY_FUN9.pin_10, KEY_FUN7.pin_1, KEY_FUN7.pin_9, KEY_FUN7.pin_10, KEY_FUN5.pin_1, KEY_FUN5.pin_9, KEY_FUN5.pin_10, KEY_FUN3.pin_1, KEY_FUN3.pin_9, KEY_FUN3.pin_10, KEY_FUN1.pin_1, KEY_FUN1.pin_9, KEY_FUN1.pin_10, LED1.pin3, LED1.pin4
  N6: KEY_FUN9.pin_4, KEY_FUN7.pin_4, KEY_FUN5.pin_4, KEY_FUN3.pin_4, KEY_FUN1.pin_4, COL.pin2
  N7: KEY_FUN9.pin_6, KEY_FUN9.pin_7, KEY_FUN7.pin_6, KEY_FUN7.pin_7, KEY_FUN5.pin_6, KEY_FUN5.pin_7, KEY_FUN3.pin_6, KEY_FUN3.pin_7, KEY_FUN3.pin_8, KEY_FUN1.pin_6, KEY_FUN1.pin_7, LED1.pin2
  N8: KEY_FUN7.pin_2, KEY_FUN8.pin_2, ROW.pin4
  N9: KEY_FUN5.pin_2, KEY_FUN6.pin_2, ROW.pin3
  N10: KEY_FUN4.pin_2, KEY_FUN3.pin_2, ROW.pin2
  N11: KEY_FUN1.pin_2, KEY_FUN2.pin_2, ROW.pin1
